# Fritzing sketch car-light-reminder (saved by Fritzing 0.9.10b)
breadboards: 1

parts:
  U1 = Mini-360 DC-DC Buck converter [package=THT]
  SP1 = SPEAKER [package=pcb_mount_speaker]
  JP1 = Header 2 [package=jst-2-pth]
  IC1 = Arduino Pro Mini (5V)
  R6 = Resistor [tolerance=±5% resistance=5.1k package="0805 [SMD]"]
  R7 = Resistor [tolerance=±5% resistance=20k package="0805 [SMD]"]
  R8 = Resistor [tolerance=±5% resistance=5.1k package="0805 [SMD]"]
  R9 = Resistor [tolerance=±5% resistance=10k package="0805 [SMD]"]
  R10 = Resistor [tolerance=±5% resistance=10k package="0805 [SMD]"]

nets:
  GND: U1.IN-, U1.OUT-, SP1.-, R8.Pin_0
  12V: U1.IN+, R9.Pin_1
  3.3V: U1.OUT+, IC1.VCC
  N1: SP1.+, IC1.D9
  IGNITION: JP1.1, R7.Pin_1
  DOOR SWITCH: JP1.2, R9.Pin_0, R10.Pin_1
  N2: IC1.GND, R6.Pin_0
  N3: IC1.D8, R8.Pin_1, R10.Pin_0
  N4: IC1.D6, R6.Pin_1, R7.Pin_0

custom parts:
  Mini-360 DC-DC Buck converter: Mini-360 DC-DC Buck converter. Tiny buck step down voltage converter, input voltage 4.75 to 23V output 1 to 17V adjustable. Available from ebay and the like.
